// Logisim project MUL.circ as structural Verilog: 1 circuit, main circuit main
module main (
  input  A,
  input  B,
  input  S1,
  input  S1_2,
  output Result,
  output C_out
);

  wire and_1_out, and_2_out, and_3_out, and_4_out, or_1_out, or_2_out, xor_1_out, xor_2_out, xor_3_out;

  xor xor_1 (xor_1_out, and_2_out, B);
  xor xor_2 (xor_2_out, xor_1_out, A);
  and and_1 (and_1_out, xor_1_out, A);
  and and_2 (and_2_out, S1_2, S1);
  and and_3 (and_3_out, A, B);
  or or_1 (or_1_out, A, B);
  xor xor_3 (xor_3_out, xor_2_out, and_2_out);
  and and_4 (and_4_out, xor_2_out, and_2_out);
  or or_2 (or_2_out, and_4_out, and_1_out);
  Multiplexer #(.select(2)) multiplexer_1 (
    .in0(and_3_out), .in1(or_1_out), .in2(xor_3_out), .in3(xor_3_out), .out(Result), .sel({S1, S1_2}));  // open: en
  and and_5 (C_out, S1, or_2_out);

  // Notes on the sheet:
  //   Task 1
  //   Inputs
  //   Cin
  //   C1
  //   sum1
  //   Full Adder
  //   S0
  //   Select Lines
  //   Bit Codes
  //   S0
  //   0    0-->AND
  //   0    1-->OR
  //   1    0-->ADD
  //   1    1-->SUB
endmodule
